// Logisim project PROYECTO1_ARQUITECURA (1) (1).circ as structural Verilog: 8 circuits, main circuit main
module main (
  input  start,
  input  U,
  input  V,
  input  W,
  input  X,
  input  Y,
  input  Z
);

  wire a, a1, a2, a3, a4, b, b1, b2, b3, b4, c, c1, c2, c3, c4, ciclo_1_a, ciclo_1_b, ciclo_1_c, ciclo_1_d,
       ciclo_1_e, ciclo_1_f, control_movimiento_1_go, control_movimiento_1_left, control_movimiento_1_right,
       control_movimiento_1_stop, d, d1, d2, d3, d4, e, e1, e2, e3, e4, f, f1, f2, f3, f4, g, g1, g2, g3,
       numeros_validos_1_a, numeros_validos_1_b, numeros_validos_1_c, numeros_validos_1_confirmacion,
       numeros_validos_1_d, numeros_validos_1_e, numeros_validos_1_f;

  CICLO ciclo_1 (
    .U(a4), .V(b4), .W(c4), .X(d4), .Y(e4), .Z(f4), .START(start), .a(ciclo_1_a), .b(ciclo_1_b),
    .c(ciclo_1_c), .d(ciclo_1_d), .e(ciclo_1_e), .f(ciclo_1_f));
  _7_Segment_Display u_7_segment_display_1 (.g(g1), .f(f1), .a(a1), .b(b1), .e(e1), .d(d1), .c(c1));  // open: dp
  _7_Segment_Display u_7_segment_display_2 (.g(g), .f(f), .a(a), .b(b), .e(e), .d(d), .c(c));  // open: dp
  NUMEROS_VALIDOS numeros_validos_1 (
    .U(U), .V(V), .W(W), .X(X), .Y(Y), .Z(Z), .A(numeros_validos_1_a), .B(numeros_validos_1_b),
    .C(numeros_validos_1_c), .D(numeros_validos_1_d), .E(numeros_validos_1_e), .F(numeros_validos_1_f),
    .CONFIRMACION(numeros_validos_1_confirmacion));
  CONTROL_MOVIMIENTO control_movimiento_1 (
    .U(numeros_validos_1_a), .V(numeros_validos_1_b), .W(numeros_validos_1_c), .X(numeros_validos_1_d),
    .Y(numeros_validos_1_e), .Z(numeros_validos_1_f), .Right(control_movimiento_1_right),
    .Left(control_movimiento_1_left), .Go(control_movimiento_1_go), .Stop(control_movimiento_1_stop));
  LED Derecha (.in(control_movimiento_1_right));
  LED Izquierda (.in(control_movimiento_1_left));
  LED Avanza (.in(control_movimiento_1_go));
  LED Para (.in(control_movimiento_1_stop));
  LED NUMERO_NO_VALIDO (.in(numeros_validos_1_confirmacion));
  Numero_Siguiente numero_siguiente_1 (
    .U(numeros_validos_1_a), .V(numeros_validos_1_b), .W(numeros_validos_1_c), .X(numeros_validos_1_d),
    .Y(numeros_validos_1_e), .Z(numeros_validos_1_f), .A(a4), .B(b4), .C(c4), .D(d4), .E(e4), .F(f4));
  _7_Segment_Display u_7_segment_display_3 (.g(g3), .f(f3), .a(a3), .b(b3), .e(e3), .d(d3), .c(c3));  // open: dp
  _7_Segment_Display u_7_segment_display_4 (.g(g2), .f(f2), .a(a2), .b(b2), .e(e2), .d(d2), .c(c2));  // open: dp
  BINARIO_TO_7SEG binario_to_7seg_1 (
    .U(numeros_validos_1_a), .V(numeros_validos_1_b), .W(numeros_validos_1_c), .X(numeros_validos_1_d),
    .Y(numeros_validos_1_e), .Z(numeros_validos_1_f), .a(a), .b(b), .c(c), .d(d), .e(e), .f(f), .g(g),
    .a1(a1), .b1(b1), .c1(c1), .d1(d1), .e1(e1), .f1(f1), .g1(g1));
  BINARIO_TO_7SEG binario_to_7seg_2 (
    .U(a4), .V(b4), .W(c4), .X(d4), .Y(e4), .Z(f4), .a(a2), .b(b2), .c(c2), .d(d2), .e(e2), .f(f2), .g(g2),
    .a1(a3), .b1(b3), .c1(c3), .d1(d3), .e1(e3), .f1(f3), .g1(g3));

  // Notes on the sheet:
  //   32
  //   16
  //   8
  //   4
  //   2
  //   1
  //   NUMERO ACTUAL
  //   SIGUIENTE NUMERO
endmodule

module BCD_to_7seg (
  input  W,
  input  X,
  input  Y,
  input  Z,
  output a,
  output b,
  output c,
  output d,
  output e,
  output f,
  output g
);

  wire and_1_out, and_2_out, and_3_out, and_4_out, and_5_out, and_6_out, and_7_out, and_8_out, and_9_out,
       and_10_out, and_11_out, and_12_out, and_13_out, and_14_out, and_15_out, and_16_out, and_17_out;

  and and_1 (and_1_out, X, Z);
  and and_2 (and_2_out, ~X, ~Z);  // AND_Gate
  and and_3 (and_3_out, Y, Z);
  and and_4 (and_4_out, ~Y, ~Z);  // AND_Gate
  and and_5 (and_5_out, Z, Y);
  and and_6 (and_6_out, ~X, ~Z);  // AND_Gate
  and and_7 (and_7_out, Y, ~Z);  // AND_Gate
  and and_8 (and_8_out, X, ~Y, Z);  // AND_Gate
  and and_9 (and_9_out, ~W, ~X, Y);  // AND_Gate
  and and_10 (and_10_out, ~X, ~Z);  // AND_Gate
  and and_11 (and_11_out, Y, ~Z);  // AND_Gate
  and and_12 (and_12_out, ~Y, ~Z);  // AND_Gate
  and and_13 (and_13_out, ~W, X, ~Y);  // AND_Gate
  and and_14 (and_14_out, ~W, X, ~Z);  // AND_Gate
  and and_15 (and_15_out, X, ~Y);  // AND_Gate
  and and_16 (and_16_out, ~X, Y);  // AND_Gate
  and and_17 (and_17_out, Y, ~Z);  // AND_Gate
  or or_1 (a, W, and_1_out, Y, and_2_out);
  or or_2 (b, ~X, and_3_out, and_4_out);  // OR_Gate
  or or_3 (c, X, ~Y, and_5_out);  // OR_Gate
  or or_4 (d, W, and_6_out, and_7_out, and_8_out, and_9_out);
  or or_5 (e, and_10_out, and_11_out);
  or or_6 (f, W, and_12_out, and_13_out, and_14_out);
  or or_7 (g, W, and_15_out, and_16_out, and_17_out);
  _7_Segment_Display u_7_segment_display_1 (.g(g), .f(f), .a(a), .b(b), .e(e), .d(d), .c(c));  // open: dp

  // Notes on the sheet:
  //   8
  //   4
  //   2
  //   1
endmodule

module BINARIO_TO_DECIMA (
  input  U,
  input  V,
  input  W,
  input  X,
  input  Y,
  input  Z,
  output dato4,
  output dato3,
  output dato2,
  output dato1,
  output dato7,
  output dato6,
  output dato5
);

  wire and_1_out, and_2_out, and_3_out, and_4_out, and_5_out, and_6_out, and_7_out, and_8_out, and_9_out,
       and_10_out, and_11_out, and_12_out, and_13_out, and_14_out, and_15_out, and_16_out, and_17_out,
       and_18_out, and_19_out, and_20_out, and_21_out, and_22_out, and_23_out, and_24_out, and_25_out,
       and_26_out, and_27_out, and_28_out, and_29_out, and_30_out;

  and and_1 (and_1_out, U, ~W);  // AND_Gate
  and and_2 (and_2_out, ~U, W, Y);  // AND_Gate
  and and_3 (and_3_out, V, ~W, ~X);  // AND_Gate
  and and_4 (and_4_out, ~U, ~V, W, X);  // AND_Gate
  and and_5 (and_5_out, U, V, W, ~X);  // AND_Gate
  and and_6 (and_6_out, ~U, V, X);  // AND_Gate
  and and_7 (and_7_out, U, ~V, ~W);  // AND_Gate
  and and_8 (and_8_out, V, W, X);
  and and_9 (and_9_out, ~U, V, W, ~X);  // AND_Gate
  and and_10 (and_10_out, U, V);
  and and_11 (and_11_out, U, W);
  and and_12 (and_12_out, ~U, ~V, W, ~X, ~Y);  // AND_Gate
  and and_13 (and_13_out, ~U, V, ~W, ~X, Y);  // AND_Gate
  and and_14 (and_14_out, ~U, V, X, ~Y);  // AND_Gate
  and and_15 (and_15_out, U, X, Y, ~Z);  // AND_Gate
  and and_16 (and_16_out, U, V, W, Y);
  and and_17 (and_17_out, V, W, ~X, ~Y);  // AND_Gate
  and and_18 (and_18_out, U, ~V, X, ~Y);  // AND_Gate
  and and_19 (and_19_out, U, ~V, ~W, ~X, Y);  // AND_Gate
  and and_20 (and_20_out, U, V, X, Y);
  and and_21 (and_21_out, ~U, ~V, ~W, X);  // AND_Gate
  and and_22 (and_22_out, ~V, W, X, Y);  // AND_Gate
  and and_23 (and_23_out, ~U, V, ~W, ~Y);  // AND_Gate
  and and_24 (and_24_out, ~U, ~V, W, X, ~Y);  // AND_Gate
  and and_25 (and_25_out, V, ~W, ~Y);  // AND_Gate
  and and_26 (and_26_out, U, ~W, ~Y);  // AND_Gate
  and and_27 (and_27_out, ~U, V, ~W, X, Y);  // AND_Gate
  and and_28 (and_28_out, U, W, X, Y);
  and and_29 (and_29_out, U, V, W, ~X, ~Y);  // AND_Gate
  and and_30 (and_30_out, ~U, ~V, ~W, Y);  // AND_Gate
  or or_1 (dato5, and_1_out, and_2_out, and_3_out, and_4_out, and_5_out);
  or or_2 (dato6, and_6_out, and_7_out, and_8_out, and_9_out);
  or or_3 (dato7, and_10_out, and_11_out);
  or or_4 (dato4, and_12_out, and_13_out, and_14_out, and_15_out, and_16_out);
  or or_5 (dato3, and_17_out, and_18_out, and_19_out, and_20_out, and_21_out, and_22_out, and_23_out);
  or or_6 (dato2, and_24_out, and_25_out, and_26_out, and_27_out, and_28_out, and_29_out, and_30_out);

  assign dato1 = Z;

  // Other names for the same wires on the sheet: B2 = dato2; B3 = dato3; B4 = dato4; B5 = dato5; B6 = dato6;
  //   B7 = dato7

  // Notes on the sheet:
  //   10
  //   8
  //   4
  //   2
  //   20
  //   40
endmodule

module CONTROL_MOVIMIENTO (
  input  U,
  input  V,
  input  W,
  input  X,
  input  Y,
  input  Z,
  output Right,
  output Left,
  output Go,
  output Stop
);

  wire and_1_out, and_2_out, and_3_out, and_4_out, and_5_out, and_6_out, and_7_out, and_8_out, and_9_out,
       and_10_out, and_11_out, and_12_out, and_13_out, and_14_out, and_15_out, and_16_out, and_17_out,
       or_1_out, or_2_out;

  and and_1 (and_1_out, ~V, ~W, ~Y, Z);  // AND_Gate
  and and_2 (and_2_out, ~V, ~W, Y, ~Z);  // AND_Gate
  and and_3 (and_3_out, ~U, V, Y, Z);  // AND_Gate
  and and_4 (and_4_out, U, W, X);
  and and_5 (and_5_out, V, X, Z);
  and and_6 (and_6_out, U, ~W, Y, ~Z);  // AND_Gate
  and and_7 (and_7_out, U, W, Z);
  and and_8 (and_8_out, V, W, ~Y);  // AND_Gate
  and and_9 (and_9_out, ~U, ~V, ~W, ~X);  // AND_Gate
  and and_10 (and_10_out, V, ~Y, ~Z);  // AND_Gate
  and and_11 (and_11_out, ~V, ~W, ~X, Z);  // AND_Gate
  and and_12 (and_12_out, ~U, ~V, ~W, ~Y, Z);  // AND_Gate
  and and_13 (and_13_out, V, ~Y, ~Z);  // AND_Gate
  and and_14 (and_14_out, ~U, V, W, ~X);  // AND_Gate
  and and_15 (and_15_out, U, ~V, ~X, Y, ~Z);  // AND_Gate
  and and_16 (and_16_out, U, W, X);
  and and_17 (and_17_out, U, W, Y, ~Z);  // AND_Gate
  or or_1 (or_1_out, and_1_out, and_2_out, and_3_out, and_4_out, and_5_out, and_6_out, and_7_out, and_8_out, and_9_out, and_10_out);
  or or_2 (or_2_out, and_11_out, and_12_out, and_13_out, and_14_out, and_15_out, and_16_out, and_17_out);
  and and_18 (Right, or_1_out, ~or_2_out);  // AND_Gate
  and and_19 (Left, or_1_out, or_2_out);
  and and_20 (Go, ~or_1_out, ~or_2_out);  // AND_Gate
  and and_21 (Stop, ~or_1_out, or_2_out);  // AND_Gate
endmodule

module Numero_Siguiente (
  input  U,
  input  V,
  input  W,
  input  X,
  input  Y,
  input  Z,
  output A,
  output B,
  output C,
  output D,
  output E,
  output F
);

  wire and_1_out, and_2_out, and_3_out, and_4_out, and_5_out, and_6_out, and_7_out, and_8_out, and_9_out,
       and_10_out, and_11_out, and_12_out, and_13_out, and_14_out, and_15_out, and_16_out, and_17_out,
       and_18_out, and_19_out, and_20_out, and_21_out, and_22_out, and_23_out, and_24_out, and_25_out,
       and_26_out, and_27_out, and_28_out, and_29_out, and_30_out, and_31_out, and_32_out, and_33_out,
       and_34_out, and_35_out, and_36_out, and_37_out, and_38_out, and_39_out, and_40_out, and_41_out,
       and_42_out, and_43_out, and_44_out, and_45_out, and_46_out, and_47_out, and_48_out, and_49_out,
       and_50_out, and_51_out, and_52_out, and_53_out, and_54_out, and_55_out, and_56_out, and_57_out,
       and_58_out, and_59_out, and_60_out;

  and and_1 (and_1_out, ~U, ~V, X, Y);  // AND_Gate
  and and_2 (and_2_out, ~U, ~W, ~X, Y);  // AND_Gate
  and and_3 (and_3_out, V, X, ~Y);  // AND_Gate
  and and_4 (and_4_out, ~U, V, W, Z);  // AND_Gate
  and and_5 (and_5_out, U, X, ~Y, Z);  // AND_Gate
  and and_6 (and_6_out, U, ~V, W, ~X, Z);  // AND_Gate
  and and_7 (and_7_out, ~X, Y, ~Z);  // AND_Gate
  and and_8 (and_8_out, U, V, X);
  and and_9 (and_9_out, ~U, W, ~Y, ~Z);  // AND_Gate
  and and_10 (and_10_out, ~W, X, Y, ~Z);  // AND_Gate
  and and_11 (and_11_out, ~U, V, ~W, ~X, Z);  // AND_Gate
  and and_12 (and_12_out, U, ~V, W, Z);  // AND_Gate
  and and_13 (and_13_out, U, V, W, X);
  and and_14 (and_14_out, U, X, Y);
  and and_15 (and_15_out, ~U, W, Y, Z);  // AND_Gate
  and and_16 (and_16_out, ~V, ~W, X, ~Y, Z);  // AND_Gate
  and and_17 (and_17_out, ~U, V, Y, ~Z);  // AND_Gate
  and and_18 (and_18_out, U, W, ~Y, Z);  // AND_Gate
  and and_19 (and_19_out, ~U, W, Y, Z);  // AND_Gate
  and and_20 (and_20_out, V, ~W, ~Y, ~Z);  // AND_Gate
  and and_21 (and_21_out, V, X, Y, ~Z);  // AND_Gate
  and and_22 (and_22_out, U, ~W, Y);  // AND_Gate
  and and_23 (and_23_out, ~V, ~W, X, ~Y, ~Z);  // AND_Gate
  and and_24 (and_24_out, ~V, W, ~X, Z);  // AND_Gate
  and and_25 (and_25_out, U, V, Y, Z);
  and and_26 (and_26_out, U, V, X);
  and and_27 (and_27_out, ~V, ~X, Y, ~Z);  // AND_Gate
  and and_28 (and_28_out, ~U, ~V, X, ~Y, ~Z);  // AND_Gate
  and and_29 (and_29_out, ~V, W, ~X);  // AND_Gate
  and and_30 (and_30_out, ~X, ~Y, ~Z);  // AND_Gate
  and and_31 (and_31_out, U, ~W, ~Y, ~Z);  // AND_Gate
  and and_32 (and_32_out, U, ~V, ~W, Y);  // AND_Gate
  and and_33 (and_33_out, V, ~W, ~Y, Z);  // AND_Gate
  and and_34 (and_34_out, V, W, Y, Z);
  and and_35 (and_35_out, ~U, W, Y, ~Z);  // AND_Gate
  and and_36 (and_36_out, ~V, ~W, X, Y);  // AND_Gate
  and and_37 (and_37_out, ~U, ~W, ~X, Z);  // AND_Gate
  and and_38 (and_38_out, ~V, ~W, ~X, Z);  // AND_Gate
  and and_39 (and_39_out, W, X, ~Y, Z);  // AND_Gate
  and and_40 (and_40_out, V, ~W, ~X, Z);  // AND_Gate
  and and_41 (and_41_out, V, W, ~Y, ~Z);  // AND_Gate
  and and_42 (and_42_out, U, ~V, ~W, ~X, Y);  // AND_Gate
  and and_43 (and_43_out, U, ~V, X, ~Y);  // AND_Gate
  and and_44 (and_44_out, ~V, W, Y, ~Z);  // AND_Gate
  and and_45 (and_45_out, ~U, ~V, W, ~X);  // AND_Gate
  and and_46 (and_46_out, U, ~W, Y, Z);  // AND_Gate
  and and_47 (and_47_out, U, ~V, W, X);  // AND_Gate
  and and_48 (and_48_out, ~U, ~V, ~X, ~Y, ~Z);  // AND_Gate
  and and_49 (and_49_out, ~W, ~X, ~Y, Z);  // AND_Gate
  and and_50 (and_50_out, ~U, ~V, ~W, ~Y);  // AND_Gate
  and and_51 (and_51_out, ~V, X, Y, Z);  // AND_Gate
  and and_52 (and_52_out, ~U, ~V, ~W, X);  // AND_Gate
  and and_53 (and_53_out, V, ~W, ~X, Y);  // AND_Gate
  and and_54 (and_54_out, ~U, V, W, ~X);  // AND_Gate
  and and_55 (and_55_out, U, ~W, ~X, Y);  // AND_Gate
  and and_56 (and_56_out, U, ~V, W);  // AND_Gate
  and and_57 (and_57_out, U, W, X);
  and and_58 (and_58_out, U, W, Y, Z);
  and and_59 (and_59_out, ~U, V, Y, ~Z);  // AND_Gate
  and and_60 (and_60_out, ~V, ~W, X, ~Y);  // AND_Gate
  or or_1 (A, and_1_out, and_2_out, and_3_out, and_4_out, and_5_out, and_6_out, and_7_out, and_8_out);
  or or_2 (B, and_9_out, and_10_out, and_11_out, and_12_out, and_13_out, and_14_out, and_15_out, and_16_out, and_17_out, and_18_out);
  or or_3 (C, and_19_out, and_20_out, and_21_out, and_22_out, and_23_out, and_24_out, and_25_out, and_26_out, and_27_out, and_28_out);
  or or_4 (D, and_29_out, and_30_out, and_31_out, and_32_out, and_33_out, and_34_out, and_35_out, and_36_out, and_37_out, and_38_out);
  or or_5 (E, and_39_out, and_40_out, and_41_out, and_42_out, and_43_out, and_44_out, and_45_out, and_46_out, and_47_out, and_48_out, and_49_out);
  or or_6 (F, and_50_out, and_51_out, and_52_out, and_53_out, and_54_out, and_60_out, and_55_out, and_56_out, and_57_out, and_58_out, and_59_out);
endmodule

module BINARIO_TO_7SEG (
  input  U,
  input  V,
  input  W,
  input  X,
  input  Y,
  input  Z,
  output a,
  output b,
  output c,
  output d,
  output e,
  output f,
  output g,
  output a1,
  output b1,
  output c1,
  output d1,
  output e1,
  output f1,
  output g1
);

  wire binario_to_decima_1_dato1, binario_to_decima_1_dato2, binario_to_decima_1_dato3,
       binario_to_decima_1_dato4, binario_to_decima_1_dato5, binario_to_decima_1_dato6,
       binario_to_decima_1_dato7;

  BINARIO_TO_DECIMA binario_to_decima_1 (
    .U(U), .V(V), .W(W), .X(X), .Y(Y), .Z(Z), .dato4(binario_to_decima_1_dato4),
    .dato3(binario_to_decima_1_dato3), .dato2(binario_to_decima_1_dato2), .dato1(binario_to_decima_1_dato1),
    .dato7(binario_to_decima_1_dato7), .dato6(binario_to_decima_1_dato6), .dato5(binario_to_decima_1_dato5));
  BCD_to_7seg bcd_to_7seg_1 (
    .W(binario_to_decima_1_dato4), .X(binario_to_decima_1_dato3), .Y(binario_to_decima_1_dato2),
    .Z(binario_to_decima_1_dato1), .a(a), .b(b), .c(c), .d(d), .e(e), .f(f), .g(g));
  BCD_to_7seg bcd_to_7seg_2 (
    .X(binario_to_decima_1_dato7), .Y(binario_to_decima_1_dato6), .Z(binario_to_decima_1_dato5), .a(a1),
    .b(b1), .c(c1), .d(d1), .e(e1), .f(f1), .g(g1));  // open: W
endmodule

module NUMEROS_VALIDOS (
  input  U,
  input  V,
  input  W,
  input  X,
  input  Y,
  input  Z,
  output A,
  output B,
  output C,
  output D,
  output E,
  output F,
  output CONFIRMACION
);

  wire and_1_out, and_2_out, and_3_out, and_4_out, and_5_out, and_6_out, and_7_out, and_8_out, and_9_out,
       and_10_out, and_11_out, and_12_out, and_13_out;

  and and_1 (and_1_out, ~U, ~V, ~W, ~X, ~Y, Z);  // AND_Gate
  and and_2 (and_2_out, ~U, ~V, W, ~X, ~Z);  // AND_Gate
  and and_3 (and_3_out, ~U, V, ~X, Y, ~Z);  // AND_Gate
  and and_4 (and_4_out, ~U, V, ~W, X, ~Y);  // AND_Gate
  and and_5 (and_5_out, ~U, V, W, Y, Z);  // AND_Gate
  and and_6 (and_6_out, U, ~V, ~W, Y, Z);  // AND_Gate
  and and_7 (and_7_out, U, ~V, W, X, ~Y, Z);  // AND_Gate
  and and_8 (and_8_out, U, ~V, W, ~X, Y);  // AND_Gate
  and and_9 (and_9_out, U, W, X, Y, ~Z);  // AND_Gate
  and and_10 (and_10_out, U, V, ~W, ~X, ~Y);  // AND_Gate
  and and_11 (and_11_out, U, V, X, Y, ~Z);  // AND_Gate
  and and_12 (and_12_out, U, V, ~Y, ~Z);  // AND_Gate
  and and_13 (and_13_out, U, V, W, X, Y, Z);
  or or_1 (CONFIRMACION, and_1_out, and_2_out, and_3_out, and_4_out, and_5_out, and_6_out, and_7_out, and_8_out, and_9_out, and_10_out, and_11_out, and_12_out, and_13_out);
  and and_14 (A, ~CONFIRMACION, U);  // AND_Gate
  and and_15 (B, ~CONFIRMACION, V);  // AND_Gate
  and and_16 (C, ~CONFIRMACION, W);  // AND_Gate
  and and_17 (D, ~CONFIRMACION, X);  // AND_Gate
  and and_18 (E, ~CONFIRMACION, Y);  // AND_Gate
  and and_19 (F, ~CONFIRMACION, Z);  // AND_Gate
endmodule

module CICLO (
  input  U,
  input  V,
  input  W,
  input  X,
  input  Y,
  input  Z,
  input  START,
  output a,
  output b,
  output c,
  output d,
  output e,
  output f
);

  wire and_1_out, clock_1_out;

  Clock #(.highDuration(5)) clock_1 (.out(clock_1_out));
  and and_1 (and_1_out, clock_1_out, START);
  D_Flip_Flop d_ff_1 (.D(U), .clk(and_1_out), .Q(a));  // open: Qn, preset, reset
  D_Flip_Flop d_ff_2 (.D(V), .clk(and_1_out), .Q(b));  // open: Qn, preset, reset
  D_Flip_Flop d_ff_3 (.D(W), .clk(and_1_out), .Q(c));  // open: Qn, preset, reset
  D_Flip_Flop d_ff_4 (.D(X), .clk(and_1_out), .Q(d));  // open: Qn, preset, reset
  D_Flip_Flop d_ff_5 (.D(Y), .clk(and_1_out), .Q(e));  // open: Qn, preset, reset
  D_Flip_Flop d_ff_6 (.D(Z), .clk(and_1_out), .Q(f));  // open: Qn, preset, reset
endmodule
