// Logisim project PROYECTO1_ARQUITECURA (1).circ as structural Verilog: 5 circuits, main circuit main
module main (
  input  U,
  input  V,
  input  W,
  input  X,
  input  Y,
  input  Z
);

  wire a, a1, b, b1, binario_to_decima_1_dato1, binario_to_decima_1_dato2, binario_to_decima_1_dato3,
       binario_to_decima_1_dato4, binario_to_decima_1_dato5, binario_to_decima_1_dato6,
       binario_to_decima_1_dato7, c, c1, d, d1, e, e1, f, f1, g, g1;

  BINARIO_TO_DECIMA binario_to_decima_1 (
    .U(U), .V(V), .W(W), .X(X), .Y(Y), .Z(Z), .dato4(binario_to_decima_1_dato4),
    .dato3(binario_to_decima_1_dato3), .dato2(binario_to_decima_1_dato2), .dato1(binario_to_decima_1_dato1),
    .dato7(binario_to_decima_1_dato7), .dato6(binario_to_decima_1_dato6), .dato5(binario_to_decima_1_dato5));
  _7_Segment_Display u_7_segment_display_1 (.g(g1), .f(f1), .a(a1), .b(b1), .e(e1), .d(d1), .c(c1));  // open: dp
  _7_Segment_Display u_7_segment_display_2 (.g(g), .f(f), .a(a), .b(b), .e(e), .d(d), .c(c));  // open: dp
  BCD_to_7seg bcd_to_7seg_1 (
    .W(binario_to_decima_1_dato4), .X(binario_to_decima_1_dato3), .Y(binario_to_decima_1_dato2),
    .Z(binario_to_decima_1_dato1), .a(a), .b(b), .c(c), .d(d), .e(e), .f(f), .g(g));
  BCD_to_7seg bcd_to_7seg_2 (
    .X(binario_to_decima_1_dato7), .Y(binario_to_decima_1_dato6), .Z(binario_to_decima_1_dato5), .a(a1),
    .b(b1), .c(c1), .d(d1), .e(e1), .f(f1), .g(g1));  // open: W
endmodule

module BCD_to_7seg (
  input  W,
  input  X,
  input  Y,
  input  Z,
  output a,
  output b,
  output c,
  output d,
  output e,
  output f,
  output g
);

  wire and_1_out, and_2_out, and_3_out, and_4_out, and_5_out, and_6_out, and_7_out, and_8_out, and_9_out,
       and_10_out, and_11_out, and_12_out, and_13_out, and_14_out, and_15_out, and_16_out, and_17_out;

  and and_1 (and_1_out, X, Z);
  and and_2 (and_2_out, ~X, ~Z);  // AND_Gate
  and and_3 (and_3_out, Y, Z);
  and and_4 (and_4_out, ~Y, ~Z);  // AND_Gate
  and and_5 (and_5_out, Z, Y);
  and and_6 (and_6_out, ~X, ~Z);  // AND_Gate
  and and_7 (and_7_out, Y, ~Z);  // AND_Gate
  and and_8 (and_8_out, X, ~Y, Z);  // AND_Gate
  and and_9 (and_9_out, ~W, ~X, Y);  // AND_Gate
  and and_10 (and_10_out, ~X, ~Z);  // AND_Gate
  and and_11 (and_11_out, Y, ~Z);  // AND_Gate
  and and_12 (and_12_out, ~Y, ~Z);  // AND_Gate
  and and_13 (and_13_out, ~W, X, ~Y);  // AND_Gate
  and and_14 (and_14_out, ~W, X, ~Z);  // AND_Gate
  and and_15 (and_15_out, X, ~Y);  // AND_Gate
  and and_16 (and_16_out, ~X, Y);  // AND_Gate
  and and_17 (and_17_out, Y, ~Z);  // AND_Gate
  or or_1 (a, W, and_1_out, Y, and_2_out);
  or or_2 (b, ~X, and_3_out, and_4_out);  // OR_Gate
  or or_3 (c, X, ~Y, and_5_out);  // OR_Gate
  or or_4 (d, W, and_6_out, and_7_out, and_8_out, and_9_out);
  or or_5 (e, and_10_out, and_11_out);
  or or_6 (f, W, and_12_out, and_13_out, and_14_out);
  or or_7 (g, W, and_15_out, and_16_out, and_17_out);
  _7_Segment_Display u_7_segment_display_1 (.g(g), .f(f), .a(a), .b(b), .e(e), .d(d), .c(c));  // open: dp

  // Notes on the sheet:
  //   8
  //   4
  //   2
  //   1
endmodule

module Binario_to_BCD (
  input  W,
  input  X,
  input  Y,
  input  Z,
  output dato1,
  output dato2,
  output dato3,
  output dato4,
  output dato5
);

  wire and_1_out, and_3_out, or_1_out, or_2_out;

  or or_1 (or_1_out, X, Y);
  and and_1 (and_1_out, W, X, ~Y);  // AND_Gate
  or or_2 (or_2_out, ~W, Y);  // OR_Gate
  and and_2 (dato4, W, ~X, ~Y);  // AND_Gate
  and and_3 (and_3_out, ~W, Y);  // AND_Gate
  or or_3 (dato2, and_3_out, and_1_out);
  and and_4 (dato3, or_2_out, X);
  and and_5 (dato5, W, or_1_out);

  assign dato1 = Z;

  // Other names for the same wires on the sheet: un = Z
endmodule

module BINARIO_TO_DECIMA (
  input  U,
  input  V,
  input  W,
  input  X,
  input  Y,
  input  Z,
  output dato4,
  output dato3,
  output dato2,
  output dato1,
  output dato7,
  output dato6,
  output dato5
);

  wire and_1_out, and_2_out, and_3_out, and_4_out, and_5_out, and_6_out, and_7_out, and_8_out, and_9_out,
       and_10_out, and_11_out, and_12_out, and_13_out, and_14_out, and_15_out, and_16_out, and_17_out,
       and_18_out, and_19_out, and_20_out, and_21_out, and_22_out, and_23_out, and_24_out, and_25_out,
       and_26_out, and_27_out, and_28_out, and_29_out, and_30_out;

  and and_1 (and_1_out, U, ~W);  // AND_Gate
  and and_2 (and_2_out, ~U, W, Y);  // AND_Gate
  and and_3 (and_3_out, V, ~W, ~X);  // AND_Gate
  and and_4 (and_4_out, ~U, ~V, W, X);  // AND_Gate
  and and_5 (and_5_out, U, V, W, ~X);  // AND_Gate
  and and_6 (and_6_out, ~U, V, X);  // AND_Gate
  and and_7 (and_7_out, U, ~V, ~W);  // AND_Gate
  and and_8 (and_8_out, V, W, X);
  and and_9 (and_9_out, ~U, V, W, ~X);  // AND_Gate
  and and_10 (and_10_out, U, V);
  and and_11 (and_11_out, U, W);
  and and_12 (and_12_out, ~U, ~V, W, ~X, ~Y);  // AND_Gate
  and and_13 (and_13_out, ~U, V, ~W, ~X, Y);  // AND_Gate
  and and_14 (and_14_out, ~U, V, X, ~Y);  // AND_Gate
  and and_15 (and_15_out, U, X, Y, ~Z);  // AND_Gate
  and and_16 (and_16_out, U, V, W, Y);
  and and_17 (and_17_out, V, W, ~X, ~Y);  // AND_Gate
  and and_18 (and_18_out, U, ~V, X, ~Y);  // AND_Gate
  and and_19 (and_19_out, U, ~V, ~W, ~X, Y);  // AND_Gate
  and and_20 (and_20_out, U, V, X, Y);
  and and_21 (and_21_out, ~U, ~V, ~W, X);  // AND_Gate
  and and_22 (and_22_out, ~V, W, X, Y);  // AND_Gate
  and and_23 (and_23_out, ~U, V, ~W, ~Y);  // AND_Gate
  and and_24 (and_24_out, ~U, ~V, W, X, ~Y);  // AND_Gate
  and and_25 (and_25_out, V, ~W, ~Y);  // AND_Gate
  and and_26 (and_26_out, U, ~W, ~Y);  // AND_Gate
  and and_27 (and_27_out, ~U, V, ~W, X, Y);  // AND_Gate
  and and_28 (and_28_out, U, W, X, Y);
  and and_29 (and_29_out, U, V, W, ~X, ~Y);  // AND_Gate
  and and_30 (and_30_out, ~U, ~V, ~W, Y);  // AND_Gate
  or or_1 (dato5, and_1_out, and_2_out, and_3_out, and_4_out, and_5_out);
  or or_2 (dato6, and_6_out, and_7_out, and_8_out, and_9_out);
  or or_3 (dato7, and_10_out, and_11_out);
  or or_4 (dato4, and_12_out, and_13_out, and_14_out, and_15_out, and_16_out);
  or or_5 (dato3, and_17_out, and_18_out, and_19_out, and_20_out, and_21_out, and_22_out, and_23_out);
  or or_6 (dato2, and_24_out, and_25_out, and_26_out, and_27_out, and_28_out, and_29_out, and_30_out);

  assign dato1 = Z;

  // Other names for the same wires on the sheet: B2 = dato2; B3 = dato3; B4 = dato4; B5 = dato5; B6 = dato6;
  //   B7 = dato7

  // Notes on the sheet:
  //   10
  //   8
  //   4
  //   2
  //   20
  //   40
endmodule

module CONTROL_MOVIMIENTO (
  input  U,
  input  V,
  input  W,
  input  X,
  input  Y,
  input  Z,
  output a,
  output b
);

  wire and_1_out, and_2_out, and_3_out, and_4_out, and_5_out, and_6_out, and_7_out, and_8_out, and_9_out,
       and_10_out, and_11_out, and_12_out, and_13_out, and_14_out, and_15_out, and_16_out, and_17_out;

  and and_1 (and_1_out, ~V, ~W, ~Y, Z);  // AND_Gate
  and and_2 (and_2_out, ~V, ~W, Y, ~Z);  // AND_Gate
  and and_3 (and_3_out, ~U, V, Y, Z);  // AND_Gate
  and and_4 (and_4_out, U, W, X);
  and and_5 (and_5_out, V, X, Z);
  and and_6 (and_6_out, U, ~W, Y, ~Z);  // AND_Gate
  and and_7 (and_7_out, U, W, Z);
  and and_8 (and_8_out, V, W, ~Y);  // AND_Gate
  and and_9 (and_9_out, ~U, ~V, ~W, ~X);  // AND_Gate
  and and_10 (and_10_out, V, ~Y, ~Z);  // AND_Gate
  and and_11 (and_11_out, ~V, ~W, ~X, Z);  // AND_Gate
  and and_12 (and_12_out, ~U, ~V, ~W, ~Y, Z);  // AND_Gate
  and and_13 (and_13_out, X, ~Y, ~Z);  // AND_Gate
  and and_14 (and_14_out, ~U, V, W, ~X);  // AND_Gate
  and and_15 (and_15_out, U, ~V, ~X, Y, ~Z);  // AND_Gate
  and and_16 (and_16_out, U, W, X);
  and and_17 (and_17_out, U, W, Y, ~Z);  // AND_Gate
  or or_1 (a, and_1_out, and_2_out, and_3_out, and_4_out, and_5_out, and_6_out, and_7_out, and_8_out, and_9_out, and_10_out);
  or or_2 (b, and_11_out, and_12_out, and_13_out, and_14_out, and_15_out, and_16_out, and_17_out);
endmodule
